# Fritzing sketch NodeMCU_OLED1306_RC522 (saved by Fritzing 0.9.6b)
breadboards: 1

parts:
  U1 = NodeMCU V3.0
  U2 = RFID RC522 SIP - 8 pins [chip_label="RFID RC522" package="SIP (Single Inline) [THT]"]
  o1 = Module display OLED I2C 128x64 SSD1306 [package=THT]

nets:
  N1: U1.D1, o1.VCC
  N2: U1.D2, o1.GND
  N3: U1.D3, U2.RST
  N4: U1.D5, U2.SCK
  N5: U1.D6, U2.MISO
  N6: U1.D7, U2.MOSI
  N7: U1.D8, U2.NSS
  GND: U1.GND, U2.GND, o1.SDA
  3V3: U1.3V3, U2.VCC, o1.SCL

custom parts:
  NodeMCU V3.0: ESP8266 based NodeMCU
  RFID RC522 SIP - 8 pins: A SIP stand-in part for RFID RC522 . With 8 pins on a 300 mil single inline package (SIP) footprint.
  Module display OLED I2C 128x64 SSD1306: Ecran OLED I2C SSD163 de 128x64 avec connexion I2C
